# Fritzing sketch SlimeVR Tracker Aux  v6 (saved by Fritzing 0.9.9b)
circuit board: 2.7cm x 3.2cm

parts:
  M1 = gy9250
  U1 = RJ45 Jack [package=rj45-8]

nets:
  N1: M1.pin1, U1.3
  N2: M1.pin2, U1.4
  N3: M1.pin3, U1.7
  N4: M1.pin4, U1.8
  N5: M1.pin7, U1.2

notes:
  Tygr Labs
  Slime VR
  Aux v6
  FSYNC/PS0
  NCS/PS1
  INT/RST
  AD0/INT
  ECL/CS
  EDA/AD0
  SDA
  SCL
  GND
  VCC

custom parts:
  gy9250: MPU-9250 module (three-axis gyroscope + three-axis acceleration + three-axis magnetic field). The generic model from ebay et. al. rather than the Sparkfun version.
  RJ45 Jack: RJ45 Jack Simple RJ45, 8-pin connection - connector for common Cat5, Cat5e, and Cat6 Ethernet cables. Footprint not yet proven in production. Connector sku is PRT-00643; Breakout PCB sku is BOB-00716. Amphenol 54602-908LF
