# Fritzing sketch SlimeVR Tracker Pimoroni Aux  v1 (saved by Fritzing 0.9.9b)
circuit board: 2cm x 3.4cm

parts:
  U1 = RJ45 Jack [package=rj45-8]
  M2 = pimoroni ICP-10125 Air Pressure Sensor Breakout [package=THT]

nets:
  N1: U1.3, M2.2-6V
  N2: U1.4, M2.GND
  N3: U1.7, M2.SCL
  N4: U1.8, M2.SDA

notes:
  Tygr Labs
  Slime VR
  Pimoroni
  SDA
  SCL
  GND
  VCC
  Aux v1

custom parts:
  RJ45 Jack: RJ45 Jack Simple RJ45, 8-pin connection - connector for common Cat5, Cat5e, and Cat6 Ethernet cables. Footprint not yet proven in production. Connector sku is PRT-00643; Breakout PCB sku is BOB-00716. Amphenol 54602-908LF
  pimoroni ICP-10125 Air Pressure Sensor Breakout: pimoroni ICP-10125 Air Pressure Sensor Breakout.
