# Fritzing sketch SlimeVR Tracker Pimoroni v1 (saved by Fritzing 0.9.9b)
circuit board: 4.5cm x 5.5cm

parts:
  WeMos_D1_Mini2 = WeMos D1 Mini
  TP1 = TP4056 [chip_label=TP4056 package="DIP (Dual Inline) [THT]"]
  VCC1 = Battery
  R1 = Resistor [tolerance=±5% power=0.25 resistance=180k package=THT]
  D2 = Schottky Diode [part_number=1N5817 package="300 mil [THT]"]
  D1 = Schottky Diode [part_number=1N5817 package="300 mil [THT]"]
  U1 = RJ45 Jack [package=rj45-8]
  M2 = pimoroni ICP-10125 Air Pressure Sensor Breakout [package=THT]

nets:
  N1: WeMos_D1_Mini2.3V3, U1.3, M2.2-6V
  N2: WeMos_D1_Mini2.5V, D2.cathode, D1.cathode
  N3: WeMos_D1_Mini2.A0, R1.Pin_1
  N4: WeMos_D1_Mini2.D1, U1.7, M2.SCL
  N5: WeMos_D1_Mini2.D2, U1.8, M2.SDA
  N6: WeMos_D1_Mini2.G, U1.4, M2.GND
  N7: TP1.pin1, D2.anode
  N8: TP1.pin3, D1.anode
  N9: TP1.pin4, VCC1.+, R1.Pin_0
  N10: TP1.pin5, VCC1.-

notes:
  -
  +
  Tygr Labs
  Slime VR v1
  VCC
  GND
  SCL
  SDA
  R1
  D1
  D2
  PWR
  Pimoroni

custom parts:
  TP4056: A DIP stand-in part for whatever IC you want. With 6 pins on a 300mil dual inline package (DIP) footprint.
  pimoroni ICP-10125 Air Pressure Sensor Breakout: pimoroni ICP-10125 Air Pressure Sensor Breakout.
