# Fritzing sketch SlimeVR Tracker v6 (saved by Fritzing 0.9.9b)
circuit board: 4.5cm x 5cm

parts:
  WeMos_D1_Mini2 = WeMos D1 Mini
  TP1 = TP4056 [chip_label=TP4056 package="DIP (Dual Inline) [THT]"]
  VCC1 = Battery
  M1 = gy9250
  R1 = Resistor [tolerance=±5% power=0.25 resistance=180k package=THT]
  D2 = Schottky Diode [part_number=1N5817 package="300 mil [THT]"]
  D1 = Schottky Diode [part_number=1N5817 package="300 mil [THT]"]
  SJ3 = Solder Jumper [package=sj_2s-no]
  SJ2 = Solder Jumper [package=sj_2s-no]
  U1 = RJ45 Jack [package=rj45-8]
  SJ4 = Solder Jumper [package=sj_3_paste2_3]

nets:
  N1: WeMos_D1_Mini2.3V3, M1.pin1, U1.3, SJ4.3
  N2: WeMos_D1_Mini2.5V, D2.cathode, D1.cathode
  N3: WeMos_D1_Mini2.A0, R1.Pin_1
  N4: WeMos_D1_Mini2.D1, M1.pin3, U1.7
  N5: WeMos_D1_Mini2.D2, M1.pin4, U1.8
  N6: WeMos_D1_Mini2.D5, SJ3.1
  N7: WeMos_D1_Mini2.D6, SJ4.1
  N8: WeMos_D1_Mini2.G, M1.pin2, SJ2.1, U1.4
  N9: TP1.pin1, D2.anode
  N10: TP1.pin3, D1.anode
  N11: TP1.pin4, VCC1.+, R1.Pin_0
  N12: TP1.pin5, VCC1.-
  N13: M1.pin5, SJ2.2
  N14: M1.pin7, SJ3.2
  N15: U1.2, SJ4.2

notes:
  -
  +
  Tygr Labs
  Slime VR v6
  VCC
  GND
  SCL
  SDA
  EDA/AD0
  ECL/CS
  AD0/INT
  INT/RST
  NCS/PS1
  FSYNC/PS0
  R1
  D1
  D2
  Solder for BNO
  PWR
  MPU BNO

custom parts:
  TP4056: A DIP stand-in part for whatever IC you want. With 6 pins on a 300mil dual inline package (DIP) footprint.
  gy9250: MPU-9250 module (three-axis gyroscope + three-axis acceleration + three-axis magnetic field). The generic model from ebay et. al. rather than the Sparkfun version.
